# Fritzing sketch Sketch (saved by Fritzing 0.9.9b)
breadboards: 1

parts:
  LED = Mini 8x8 LED Matrix Backpack [part_number=872]
  Sensor = DFRobot Capacitive Soil Moisture Sensor V1.0 [part_number=SEN0193]
  Bauteil1 = Arduino Micro (Rev3)
  BH1750FVI_Breakout1 = BH1750 (GY-302) Breakout Board [part_number=BH1750FVI]
  AM1 = AM2302 Humidity and Temperature Sensor
  HC-SR04_Sensor_1 = HC-SR04 Ultrasonic Distance Sensor

nets:
  N1: LED.SCL, Bauteil1.D3/SCL, BH1750FVI_Breakout1.SCL
  N2: LED.SDA, Bauteil1.D2/SDA, BH1750FVI_Breakout1.SDA
  GND: LED.GND, Sensor.GND, Bauteil1.GND, BH1750FVI_Breakout1.GND, AM1.GND, HC-SR04_Sensor_1.GND
  VCC: LED.VDD, Sensor.VCC, Bauteil1.5V, BH1750FVI_Breakout1.VCC, AM1.VDD, HC-SR04_Sensor_1.VCC
  N3: Sensor.A, Bauteil1.A0
  N4: Bauteil1.D10_PWM/A10, HC-SR04_Sensor_1.ECHO
  N5: Bauteil1.D11_PWM, HC-SR04_Sensor_1.TRIG
  N6: Bauteil1.D12_PWM/A11, AM1.DATA

custom parts:
  Mini 8x8 LED Matrix Backpack: This 0.8" 8x8 monochrome LED matrix includes a driver chip for simple control via an I2C interface. The backpack features address-selection jumpers so you can connect up to four matrices on a single I2C bus.
  DFRobot Capacitive Soil Moisture Sensor V1.0: DFRobot Capacitive Soil Moisture Sensor V1.0 This product measures soil moisture levels by capacitive sensing, rather than resistive sensing like other types of moisture sensor. It is made of a corrosion resistant material giving it a long service life. Insert it into soil and impress your friends with the real-time soil moisture data! The product includes an on-board voltage regulator which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
  BH1750 (GY-302) Breakout Board: The ROHM Semiconductor BH1750FVI is a digital ambient light sensor for the I2C bus interface. The BH750FVI is able to detect a wide range of light intensities (1-65535 lux). The spectral range is similar to that of the human eye.
