# Fritzing sketch SketchRaspberryPi4 (saved by Fritzing 0.9.9b)
breadboards: 1

parts:
  LED = Mini 8x8 LED Matrix Backpack [part_number=872]
  Sensor = DFRobot Capacitive Soil Moisture Sensor V1.0 [part_number=SEN0193]
  BH1750FVI_Breakout1 = BH1750 (GY-302) Breakout Board [part_number=BH1750FVI]
  AM1 = AM2302 Humidity and Temperature Sensor
  HC-SR04_Sensor_1 = HC-SR04 Ultrasonic Distance Sensor
  MCU1 = Raspberry Pi Zero
  R2 = Resistor [tolerance=±5% power=0.25 resistance=330 package=THT]
  R3 = Resistor [tolerance=±5% power=0.25 resistance=10k package=THT]

nets:
  N1: LED.SCL, BH1750FVI_Breakout1.SCL, MCU1.pin_5
  N2: LED.SDA, BH1750FVI_Breakout1.SDA, MCU1.pin_3
  GND: LED.GND, Sensor.GND, BH1750FVI_Breakout1.GND, AM1.GND, HC-SR04_Sensor_1.GND, MCU1.pin_6, MCU1.pin_39, R3.Pin_1
  VDD: LED.VDD, Sensor.VCC, BH1750FVI_Breakout1.VCC, AM1.VDD, MCU1.pin_1
  N3: AM1.DATA, MCU1.pin_7
  N4: HC-SR04_Sensor_1.VCC, MCU1.pin_2, MCU1.pin_4
  N5: HC-SR04_Sensor_1.TRIG, MCU1.pin_10
  N6: HC-SR04_Sensor_1.ECHO, MCU1.pin_33, R2.Pin_0
  N7: MCU1.pin_8, R2.Pin_1, R3.Pin_0

custom parts:
  Mini 8x8 LED Matrix Backpack: This 0.8" 8x8 monochrome LED matrix includes a driver chip for simple control via an I2C interface. The backpack features address-selection jumpers so you can connect up to four matrices on a single I2C bus.
  DFRobot Capacitive Soil Moisture Sensor V1.0: DFRobot Capacitive Soil Moisture Sensor V1.0 This product measures soil moisture levels by capacitive sensing, rather than resistive sensing like other types of moisture sensor. It is made of a corrosion resistant material giving it a long service life. Insert it into soil and impress your friends with the real-time soil moisture data! The product includes an on-board voltage regulator which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
  BH1750 (GY-302) Breakout Board: The ROHM Semiconductor BH1750FVI is a digital ambient light sensor for the I2C bus interface. The BH750FVI is able to detect a wide range of light intensities (1-65535 lux). The spectral range is similar to that of the human eye.
