# Fritzing sketch Sketch_dev_rpi4 (saved by Fritzing 0.9.9b)
breadboards: 1

parts:
  Arduino = Arduino Nano (Rev3.0)
  LED = Mini 8x8 LED Matrix Backpack [part_number=872]
  Sensor = DFRobot Capacitive Soil Moisture Sensor V1.0 [part_number=SEN0193]

nets:
  GND: Arduino.GND, LED.GND, Sensor.GND
  5V: Arduino.5V, LED.VDD, Sensor.VCC
  N1: Arduino.A5, LED.SCL
  N2: Arduino.A4, LED.SDA
  N3: Arduino.A0, Sensor.A

custom parts:
  Mini 8x8 LED Matrix Backpack: This 0.8" 8x8 monochrome LED matrix includes a driver chip for simple control via an I2C interface. The backpack features address-selection jumpers so you can connect up to four matrices on a single I2C bus.
  DFRobot Capacitive Soil Moisture Sensor V1.0: DFRobot Capacitive Soil Moisture Sensor V1.0 This product measures soil moisture levels by capacitive sensing, rather than resistive sensing like other types of moisture sensor. It is made of a corrosion resistant material giving it a long service life. Insert it into soil and impress your friends with the real-time soil moisture data! The product includes an on-board voltage regulator which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
